# Fritzing sketch alarmclock_mk1 (saved by Fritzing 0.9.3b)
circuit board: 2.008cm x 2.61488cm
circuit board: 1.98555cm x 0.891922cm
circuit board: 10cm x 5cm
breadboards: 2

parts:
  The_nano = Arduino Nano (Rev3.0)
  Select_Encoder = Rotary Encoder [package=THT]
  Select_Button = Pushbutton [package="[THT]"]
  J1 = Camdenboss CTB0158-4 [part_number=CTB0158-4 package=THT]
  SPKR1 = Loudspeaker
  Led_8x8_Display = LED Matrix - Serial Interface - Red/Green/Blue
  Snooze_Button = Pushbutton [package="[THT]"]
  Master_Switch = Pushbutton [package=THT]
  Amplifier = LM386 [package=dip08]
  C1 = Electrolytic Capacitor [capacitance=100µF voltage=10V package="100 mil [THT, electrolytic]"]
  C3 = Electrolytic Capacitor [capacitance=100µF package="100 mil [THT, electrolytic]"]
  P1_Volume = Rotary Potentiometer (Small) [maximum_resistance=20k package=THT]
  9_V = Power plug
  R1 = Resistor [tolerance=±5% resistance=100k package=THT]
  C2 = Ceramic Capacitor [capacitance=100nF voltage=10V package="200 mil [THT, multilayer]"]
  Phones_Out = rounded female pin header, 2 pins [form="♀ (female rounded)"]
  U1 = Voltage Regulator - 5V [package="TO220 [THT]"]
  C4 = Ceramic Capacitor [capacitance=470nF package="100 mil [THT, multilayer]"]
  C5 = Ceramic Capacitor [capacitance=100nF package="100 mil [THT, multilayer]"]
  Led_Data = male pin header, 3 pins [form="♂ (male)"]
  Led_Power = male pin header, 2 pins [form="♂ (male)"]
  Radio = Digital FM Radio Receiver
  R2 = Resistor [tolerance=±5% resistance=10k package=THT]
  LDR = Photocell (LDR) [package=THT]

nets:
  GND: The_nano.GND, Select_Encoder.EncoderPinC, Select_Button.Pin_3, Select_Button.Pin_4, J1.pin2, J1.pin3, SPKR1.pin1, Led_8x8_Display.GND, Snooze_Button.Pin_1, Snooze_Button.Pin_2, Master_Switch.leg0, Amplifier.+IN, Amplifier.V-, C3.-, P1_Volume.leg2, 9_V.GND, Phones_Out.pin2, U1.GND, C4.0, C5.1, Led_Power.pin1, Radio.GND, R2.Pin_1
  N1: The_nano.D2, Radio.!RST
  N2: The_nano.D5, Snooze_Button.Pin_3, Snooze_Button.Pin_4
  N3: The_nano.D6, Master_Switch.leg1
  N4: The_nano.D7, Select_Encoder.EncoderPinB
  N5: The_nano.D8, Select_Encoder.EncoderPinA
  N6: The_nano.D9, Select_Button.Pin_1, Select_Button.Pin_2
  N7: The_nano.D10, Led_8x8_Display.SCK, Led_Data.pin3
  N8: The_nano.D11/MOSI, Led_8x8_Display.CS, Led_Data.pin2
  N9: The_nano.D12/MISO, Led_8x8_Display.MOSI, Led_Data.pin1
  VIN: The_nano.VIN, J1.pin4, 9_V.VCC, U1.input_voltage, C4.1
  5V: The_nano.5V, Led_8x8_Display.VCC, Led_Power.pin2, LDR.pin_0
  N10: The_nano.A5, Radio.SCLK
  N11: The_nano.A4, Radio.SDIO
  N12: The_nano.A2, R2.Pin_0, LDR.pin_1
  3V3: The_nano.3V3, Radio.3.3V
  N13: J1.pin1, SPKR1.pin2, C1.-
  N14: Amplifier.-IN, C2.1
  N15: Amplifier.OUT, C1.+
  N16: Amplifier.V+, C3.+, U1.output_voltage, C5.0
  N17: P1_Volume.leg1, R1.Pin_1
  N18: P1_Volume.wiper, C2.0
  N19: R1.Pin_0, Phones_Out.pin1

notes:
  +
  -
  Vcc
  Gnd
  upper= isolated wires
  lower=dot bridges / open wires
  Layout 4 experimental board:
  connection to breadboard
